# Fritzing sketch self-service box (saved by Fritzing 0.9.3b)
circuit board: 8.46667cm x 5.64444cm
breadboards: 1

parts:
  U1 = LCD-16X2 [package=lcd-16x2]
  Part1 = Arduino Uno (Rev3) - ICSP
  R1 = Resistor [tolerance=±5% resistance=220 package="0402 [SMD]"]
  R2 = Resistor [tolerance=±5% resistance=10k package="0402 [SMD]"]
  S1 = Pushbutton [package="[THT]"]
  S2 = Pushbutton [package="[THT]"]
  R3 = Resistor [tolerance=±5% resistance=10k package="0402 [SMD]"]
  R4 = Rotary Potentiometer (Large) [maximum_resistance=100kΩ package=THT]
  J1 = Basic Servo
  C1 = Capacitor Polarized [package=cpol-radial-100uf-25v]

nets:
  GND: U1.VSS, U1.R_W, U1.K, Part1.GND, R2.Pin_0, R3.Pin_0, J1.gnd, C1.+
  VDD: U1.VDD, Part1.5V, R1.Pin_0, S1.Pin_3, S1.Pin_4, S2.Pin_3, S2.Pin_4, J1.vcc, C1.-
  N1: U1.VO, R4.wiper
  N2: U1.RS, Part1.ICSP_MISO, Part1.D12/MISO
  N3: U1.E, Part1.ICSP_MOSI, Part1.D11_PWM/MOSI
  N4: U1.DB4, Part1.D5_PWM
  N5: U1.DB5, Part1.D4
  N6: U1.DB6, Part1.D3_PWM
  N7: U1.DB7, Part1.D2
  N8: U1.A, R1.Pin_1
  N9: Part1.D9_PWM, J1.pulse
  N10: Part1.D6_PWM, R2.Pin_1, S2.Pin_1, S2.Pin_2
  N11: Part1.D7, S1.Pin_1, S1.Pin_2, R3.Pin_1

notes:
  [those 4 purple/pink color wires connected to D2,D3,D4,D5 controls the content on screen
  red lines are connected to power line and blue ones( or black) are connected to ground line
  the middle of the potentiometer connected to the third point from the left of the screen and can control the brightness of the screen
